// Logisim project ODS_3.circ as structural Verilog: 1 circuit, main circuit main
module main (
  input  A1,
  input  A2,
  input  Plus1,
  input  A,
  input  B,
  input  Plus
);

  wire and_1_out, and_2_out, and_3_out, and_4_out, and_5_out, and_6_out, and_7_out, and_8_out, and_9_out,
       and_10_out, and_11_out, and_12_out, and_13_out, and_14_out, and_15_out, and_16_out, and_17_out,
       not_1_out, not_2_out, not_3_out, not_4_out, not_5_out, not_6_out, not_7_out, not_8_out, or_1_out,
       or_2_out, or_3_out, or_4_out, or_5_out, or_6_out, xor_1_out, xor_2_out;

  not not_1 (not_1_out, A);
  not not_2 (not_2_out, Plus);
  not not_3 (not_3_out, B);
  not not_4 (not_4_out, B);
  not not_5 (not_5_out, Plus);
  not not_6 (not_6_out, A);
  not not_7 (not_7_out, B);
  not not_8 (not_8_out, B);
  and and_1 (and_1_out, not_1_out, B);
  and and_2 (and_2_out, B, not_2_out);
  and and_3 (and_3_out, A, not_3_out);
  and and_4 (and_4_out, not_4_out, not_5_out);
  and and_5 (and_5_out, not_6_out, not_7_out);
  and and_6 (and_6_out, not_8_out, Plus);
  and and_7 (and_7_out, A, B);
  and and_8 (and_8_out, B, Plus);
  and and_9 (and_9_out, and_1_out, and_2_out);
  and and_10 (and_10_out, and_3_out, and_4_out);
  and and_11 (and_11_out, and_5_out, and_6_out);
  and and_12 (and_12_out, and_7_out, and_8_out);
  or or_1 (or_1_out, and_9_out, and_10_out);
  or or_2 (or_2_out, and_11_out, and_12_out);
  and and_13 (and_13_out, A, B);
  and and_14 (and_14_out, A, Plus);
  and and_15 (and_15_out, B, Plus);
  or or_3 (or_3_out, or_1_out, or_2_out);
  or or_4 (or_4_out, and_13_out, and_14_out);
  or or_5 (or_5_out, or_4_out, and_15_out);
  LED Res (.in(or_3_out));
  LED Plus_out (.in(or_5_out));
  xor xor_1 (xor_1_out, A1, A2);
  and and_16 (and_16_out, xor_1_out, Plus1);
  and and_17 (and_17_out, A1, A2);
  xor xor_2 (xor_2_out, xor_1_out, Plus1);
  LED Res2 (.in(xor_2_out));
  LED Trun2 (.in(or_6_out));
  or or_6 (or_6_out, and_16_out, and_17_out);
endmodule
